// Logisim project CPU_DESIGN_QU.circ as structural Verilog: 5 circuits, main circuit main
module main (
  input  [15:0] Binary_to_Hex,
  output [15:0] Hex
);

  wire clock_1_out, cpu_1_done, cpu_1_mem_out_en, cpu_1_mem_write_en, Reset_out, Start_out, Stop_out;
  wire [7:0] cpu_1_mem_addr;
  wire [15:0] cpu_1_mem_in, MEMORY_dout;

  Clock clock_1 (.out(clock_1_out));
  Button Start (.out(Start_out));
  Button Stop (.out(Stop_out));
  Button Reset (.out(Reset_out));
  CPU cpu_1 (
    .clk(clock_1_out), .mem_out(MEMORY_dout), .start(Start_out), .stop(Stop_out), .reset(Reset_out),
    .mem_addr(cpu_1_mem_addr), .mem_write_en(cpu_1_mem_write_en), .mem_out_en(cpu_1_mem_out_en),
    .mem_in(cpu_1_mem_in), .done(cpu_1_done));
  LED led_1 (.in(cpu_1_done));
  RAM #(.dataWidth(16)) MEMORY (
    .addr(cpu_1_mem_addr), .we(cpu_1_mem_write_en), .oe(cpu_1_mem_out_en), .clk(clock_1_out),
    .din(cpu_1_mem_in), .dout(MEMORY_dout));

  assign Hex = Binary_to_Hex;

  // Notes on the sheet:
  //   Oa2006040
  //   TOP Level
  //   we use this to for getting the hex value of an instructiont
endmodule

module ALU (
  input  [7:0] Operand_1,
  input  [7:0] Operand_2,
  input  CLK,
  input  [3:0] Instruction,
  output [7:0] Result,
  output CF,
  output ZF
);

  wire adder_1_cout, and_2_out, and_3_out, and_4_out, and_5_out, and_6_out, controlled_buffer_11_out,
       controlled_buffer_13_out, nor_1_out, or_1_out, or_2_out, subtractor_1_bout;
  wire [7:0] adder_1_out, and_1_out, shifter_1_out, shifter_2_out, subtractor_1_out, undriven, undriven_2;
  wire [15:0] controlled_buffer_1_out, controlled_buffer_2_out, controlled_buffer_3_out,
       controlled_buffer_4_out, controlled_buffer_5_out;

  assign controlled_buffer_1_out = and_6_out ? {Operand_2, Operand_1} : 16'bz;  // Controlled_Buffer controlled_buffer_1
  assign controlled_buffer_2_out = and_5_out ? {Operand_2, Operand_1} : 16'bz;  // Controlled_Buffer controlled_buffer_2
  assign controlled_buffer_3_out = and_4_out ? {Operand_2, Operand_1} : 16'bz;  // Controlled_Buffer controlled_buffer_3
  assign controlled_buffer_4_out = and_3_out ? {undriven, Operand_2} : 16'bz;  // Controlled_Buffer controlled_buffer_4
  assign controlled_buffer_5_out = and_2_out ? {undriven_2, Operand_2} : 16'bz;  // Controlled_Buffer controlled_buffer_5
  Adder adder_1 (
    .a(controlled_buffer_1_out[7:0]), .b(controlled_buffer_1_out[15:8]), .out(adder_1_out),
    .cout(adder_1_cout));  // open: cin
  Subtractor subtractor_1 (
    .a(controlled_buffer_2_out[7:0]), .b(controlled_buffer_2_out[15:8]), .out(subtractor_1_out),
    .bout(subtractor_1_bout));  // open: bin
  assign and_1_out = controlled_buffer_3_out[7:0] & controlled_buffer_3_out[15:8];  // AND_Gate and_1, 8 bits wide
  Shifter #(.shift("lr")) shifter_1 (.in(controlled_buffer_4_out[7:0]), .\dist (3'b001), .out(shifter_1_out));
  Shifter shifter_2 (.in(controlled_buffer_5_out[7:0]), .\dist (3'b001), .out(shifter_2_out));
  assign Result = and_6_out ? adder_1_out : 8'bz;  // Controlled_Buffer controlled_buffer_6
  assign Result = and_5_out ? subtractor_1_out : 8'bz;  // Controlled_Buffer controlled_buffer_7
  assign Result = and_4_out ? and_1_out : 8'bz;  // Controlled_Buffer controlled_buffer_8
  assign Result = and_3_out ? shifter_1_out : 8'bz;  // Controlled_Buffer controlled_buffer_9
  assign Result = and_2_out ? shifter_2_out : 8'bz;  // Controlled_Buffer controlled_buffer_10
  and and_2 (and_2_out, Instruction[3], ~Instruction[2], ~Instruction[1], Instruction[0]);  // AND_Gate
  and and_3 (and_3_out, Instruction[3], ~Instruction[2], ~Instruction[1], ~Instruction[0]);  // AND_Gate
  assign controlled_buffer_11_out = and_6_out ? adder_1_cout : 1'bz;  // Controlled_Buffer controlled_buffer_11
  assign controlled_buffer_11_out = and_5_out ? subtractor_1_bout : 1'bz;  // Controlled_Buffer controlled_buffer_12
  and and_4 (and_4_out, ~Instruction[3], Instruction[2], Instruction[1], Instruction[0]);  // AND_Gate
  and and_5 (and_5_out, ~Instruction[3], Instruction[2], Instruction[1], ~Instruction[0]);  // AND_Gate
  and and_6 (and_6_out, ~Instruction[3], Instruction[2], ~Instruction[1], Instruction[0]);  // AND_Gate
  or or_1 (or_1_out, and_2_out, and_3_out, and_4_out);
  nor nor_1 (nor_1_out, Result[0], Result[1], Result[2], Result[3], Result[4], Result[5], Result[6], Result[7]);
  or or_2 (or_2_out, and_2_out, and_3_out, and_4_out, and_5_out, and_6_out);
  D_Flip_Flop d_ff_1 (.D(controlled_buffer_11_out), .clk(CLK), .Q(CF), .reset(or_1_out));  // open: Qn, preset
  D_Flip_Flop d_ff_2 (.D(controlled_buffer_13_out), .clk(CLK), .Q(ZF));  // open: Qn, preset, reset
  assign controlled_buffer_13_out = or_2_out ? nor_1_out : 1'bz;  // Controlled_Buffer controlled_buffer_13

  // Notes on the sheet:
  //   ADD
  //   SUB
  //   AND
  //   LSR
  //   LSL
  //   Enable
  //   LSL
  //   LSR
  //   AND
  //   ALU
  //   SUB
  //   ADD
endmodule

module CU (
  input  [3:0] opcode,
  input  start,
  input  stop,
  input  clk,
  output OE_PC,
  output WE_MAR,
  output INC_PC,
  output WE_RAM,
  output OE_RAM,
  output WE_IR,
  output En_Src,
  output En_Dst,
  output En_ALU_RESULT,
  output EN_IMM,
  output EN_ADDR_3_8,
  output EN_ADDR_8_3,
  output EN_RAM_OUT,
  output HLT
);

  wire not_1_out, or_1_out, ring_counter_1_out_4, ring_counter_1_out_5, ring_counter_1_out_6,
       ring_counter_1_out_7, ring_counter_1_out_8, ring_counter_1_out_9;
  wire [7:0] adder_1_out, adder_2_out, controlled_buffer_1_out, rom_2_data;
  wire [15:14] rom_1_data;

  ROM #(.dataWidth(16)) rom_1 (
    .addr(controlled_buffer_1_out),
    .data({rom_1_data, HLT, EN_RAM_OUT, EN_ADDR_8_3, EN_ADDR_3_8, EN_IMM, En_ALU_RESULT, En_Dst, En_Src, WE_IR, OE_RAM, WE_RAM, INC_PC, WE_MAR, OE_PC}));
  Ring_Counter ring_counter_1 (
    .clk(clk), .start(start), .stop(stop), .out_4(ring_counter_1_out_4), .out_5(ring_counter_1_out_5),
    .out_6(ring_counter_1_out_6), .out_7(ring_counter_1_out_7), .out_8(ring_counter_1_out_8),
    .out_9(ring_counter_1_out_9));
  ROM #(.addrWidth(4)) rom_2 (.addr(opcode), .data(rom_2_data));
  assign controlled_buffer_1_out = not_1_out ? 8'h15 : 8'bz;  // Controlled_Buffer controlled_buffer_1
  or or_1 (or_1_out, ring_counter_1_out_4, ring_counter_1_out_5, ring_counter_1_out_6, ring_counter_1_out_7, ring_counter_1_out_8, ring_counter_1_out_9);
  not not_1 (not_1_out, or_1_out);
  assign controlled_buffer_1_out = ring_counter_1_out_4 ? {8{1'b0}} : 8'bz;  // Controlled_Buffer controlled_buffer_2
  assign controlled_buffer_1_out = ring_counter_1_out_5 ? 8'h1 : 8'bz;  // Controlled_Buffer controlled_buffer_3
  assign controlled_buffer_1_out = ring_counter_1_out_6 ? 8'h2 : 8'bz;  // Controlled_Buffer controlled_buffer_4
  assign controlled_buffer_1_out = ring_counter_1_out_7 ? rom_2_data : 8'bz;  // Controlled_Buffer controlled_buffer_5
  Adder adder_1 (.a(rom_2_data), .b(8'h1), .out(adder_1_out));  // open: cin, cout
  assign controlled_buffer_1_out = ring_counter_1_out_8 ? adder_1_out : 8'bz;  // Controlled_Buffer controlled_buffer_6
  Adder adder_2 (.a(rom_2_data), .b(8'h2), .out(adder_2_out));  // open: cin, cout
  assign controlled_buffer_1_out = ring_counter_1_out_9 ? adder_2_out : 8'bz;  // Controlled_Buffer controlled_buffer_7

  // Notes on the sheet:
  //   contents of rom_1 (hex, n*v repeats v):
  //   3 10 24 c0 0 0 280 0 0 402 1410 1480 802 48 0 180 0 0 400 0 0 2000
  //   contents of rom_2 (hex, n*v repeats v):
  //   15 3 6 9 c 5*f 12
  //   CONTROL UNIT
endmodule

module Ring_Counter (
  input  clk,
  input  start,
  input  stop,
  output out_4,
  output out_5,
  output out_6,
  output out_7,
  output out_8,
  output out_9
);

  wire controlled_buffer_1_out, controlled_buffer_2_out;

  D_Flip_Flop d_ff_1 (.D(out_9), .clk(clk), .Q(out_4), .preset(controlled_buffer_2_out), .reset(stop));  // open: Qn
  assign controlled_buffer_1_out = start ? start : 1'bz;  // Controlled_Buffer controlled_buffer_1
  assign controlled_buffer_2_out = start ? controlled_buffer_1_out : 1'bz;  // Controlled_Buffer controlled_buffer_2
  assign controlled_buffer_1_out = stop ? stop : 1'bz;  // Controlled_Buffer controlled_buffer_3
  D_Flip_Flop d_ff_2 (.D(out_4), .clk(clk), .Q(out_5), .reset(controlled_buffer_1_out));  // open: Qn, preset
  D_Flip_Flop d_ff_3 (.D(out_5), .clk(clk), .Q(out_6), .reset(controlled_buffer_1_out));  // open: Qn, preset
  D_Flip_Flop d_ff_4 (.D(out_6), .clk(clk), .Q(out_7), .reset(controlled_buffer_1_out));  // open: Qn, preset
  D_Flip_Flop d_ff_5 (.D(out_7), .clk(clk), .Q(out_8));  // open: Qn, preset, reset
  D_Flip_Flop d_ff_6 (.D(out_8), .clk(clk), .Q(out_9), .reset(controlled_buffer_1_out));  // open: Qn, preset

  // Notes on the sheet:
  //   Ring_Counter
endmodule

module CPU (
  input  clk,
  input  [15:0] mem_out,
  input  start,
  input  stop,
  input  reset,
  output [7:0] mem_addr,
  output mem_write_en,
  output mem_out_en,
  output [15:0] mem_in,
  output done
);

  wire alu_1_cf, alu_1_zf, and_2_out, and_5_out, BC, BZ, decoder_1_out0, decoder_1_out1, decoder_1_out2,
       decoder_1_out3, decoder_1_out4, decoder_1_out5, decoder_1_out6, decoder_1_out7, EN_ADDR_3_8,
       EN_ADDR_8_3, En_ALU_RESULT, En_Dst, EN_IMM, EN_RAM_OUT, En_Src, HALT, INC_PC, LOAD_PC, not_1_out,
       OE_PC, or_1_out, or_2_out, or_3_out, WE_IR, WE_MAR;
  wire [2:0] Rd_MUX;
  wire [3:0] IR_q, IR_q_2, IR_q_3, IR_q_4;
  wire [7:0] alu_1_result, ALU_RESULT, LADDR_3_8, multiplexer_2_out, multiplexer_3_out, PC_q, R0_q, R1_q,
       R2_q, R3_q, R4_q, R5_q, R6_q, R7_q;
  wire [15:0] controlled_buffer_3_out, RAM_OUT;

  Counter PC (.clr(or_1_out), .load(LOAD_PC), .count(INC_PC), .clk(clk), .D(LADDR_3_8), .Q(PC_q));  // open: up, carry
  Register R0 (.D(ALU_RESULT), .en(decoder_1_out0), .clk(clk), .Q(R0_q));  // open: clr
  Register R4 (.D(ALU_RESULT), .en(decoder_1_out4), .clk(clk), .Q(R4_q));  // open: clr
  Bit_Extender #(.in_width(16), .out_width(8), .\type ("zero")) bit_extender_1 (.in(RAM_OUT), .out(ALU_RESULT));
  Register R1 (.D(ALU_RESULT), .en(decoder_1_out1), .clk(clk), .Q(R1_q));  // open: clr
  Register R5 (.D(ALU_RESULT), .en(decoder_1_out5), .clk(clk), .Q(R5_q));  // open: clr
  // Probe on ALU_RESULT
  assign LADDR_3_8 = OE_PC ? PC_q : 8'bz;  // Controlled_Buffer controlled_buffer_1
  Register MAR (.D(LADDR_3_8), .en(WE_MAR), .clk(clk), .Q(mem_addr));  // open: clr
  Register R2 (.D(ALU_RESULT), .en(decoder_1_out2), .clk(clk), .Q(R2_q));  // open: clr
  Register R6 (.D(ALU_RESULT), .en(decoder_1_out6), .clk(clk), .Q(R6_q));  // open: clr
  assign mem_in = {{8{1'b0}}, ALU_RESULT};  // Bit_Extender bit_extender_2
  Register R3 (.D(ALU_RESULT), .en(decoder_1_out3), .clk(clk), .Q(R3_q));  // open: clr
  Register R7 (.D(ALU_RESULT), .en(decoder_1_out7), .clk(clk), .Q(R7_q));  // open: clr
  or or_1 (or_1_out, HALT, reset);
  Multiplexer #(.disabled("Z"), .enable("true"), .select(3), .width(8)) multiplexer_1 (
    .in0(R0_q), .in1(R1_q), .in2(R2_q), .in3(R3_q), .in4(R4_q), .in5(R5_q), .in6(R6_q), .in7(R7_q),
    .out(ALU_RESULT), .sel(IR_q_2[2:0]), .en(En_Src));
  assign RAM_OUT = EN_RAM_OUT ? mem_out : 16'bz;  // Controlled_Buffer controlled_buffer_2
  assign controlled_buffer_3_out = WE_IR ? mem_out : 16'bz;  // Controlled_Buffer controlled_buffer_3
  or or_2 (or_2_out, reset, start);
  // Probe on LADDR_3_8
  Register #(.width(16)) IR (
    .D(controlled_buffer_3_out), .en(WE_IR), .clk(clk), .Q({IR_q[3:2], BZ, IR_q[0], IR_q_4, IR_q_3, IR_q_2}));  // open: clr
  and and_1 (done, ~IR_q[0], ~BZ, ~IR_q[2], ~IR_q[3]);  // AND_Gate
  not not_1 (not_1_out, or_2_out);
  or or_3 (or_3_out, stop, HALT);
  Decoder #(.select(3)) decoder_1 (
    .out0(decoder_1_out0), .out1(decoder_1_out1), .out2(decoder_1_out2), .out3(decoder_1_out3),
    .out4(decoder_1_out4), .out5(decoder_1_out5), .out6(decoder_1_out6), .out7(decoder_1_out7), .sel(Rd_MUX),
    .en(En_Dst));
  and and_2 (and_2_out, not_1_out, or_3_out);
  Multiplexer #(.select(3), .width(8)) multiplexer_2 (
    .in0(R0_q), .in1(R1_q), .in2(R2_q), .in3(R3_q), .in4(R4_q), .in5(R5_q), .in6(R6_q), .in7(R7_q),
    .out(multiplexer_2_out), .sel({IR_q_3[1:0], IR_q_2[3]}));
  Multiplexer #(.select(3), .width(8)) multiplexer_3 (
    .in0(R0_q), .in1(R1_q), .in2(R2_q), .in3(R3_q), .in4(R4_q), .in5(R5_q), .in6(R6_q), .in7(R7_q),
    .out(multiplexer_3_out), .sel(IR_q_2[2:0]));
  or or_4 (LOAD_PC, BZ, BC);
  CU cu_1 (
    .opcode({IR_q[3:2], BZ, IR_q[0]}), .start(or_2_out), .stop(and_2_out), .clk(clk), .OE_PC(OE_PC),
    .WE_MAR(WE_MAR), .INC_PC(INC_PC), .WE_RAM(mem_write_en), .OE_RAM(mem_out_en), .WE_IR(WE_IR),
    .En_Src(En_Src), .En_Dst(En_Dst), .En_ALU_RESULT(En_ALU_RESULT), .EN_IMM(EN_IMM),
    .EN_ADDR_3_8(EN_ADDR_3_8), .EN_ADDR_8_3(EN_ADDR_8_3), .EN_RAM_OUT(EN_RAM_OUT), .HLT(HALT));
  ALU alu_1 (
    .Operand_1(multiplexer_2_out), .Operand_2(multiplexer_3_out), .CLK(clk),
    .Instruction({IR_q[3:2], BZ, IR_q[0]}), .Result(alu_1_result), .CF(alu_1_cf), .ZF(alu_1_zf));
  assign ALU_RESULT = En_ALU_RESULT ? alu_1_result : 8'bz;  // Controlled_Buffer controlled_buffer_4
  // AND_Gate and_3 has open pins: in0=alu_1_zf, in1=IR_q[0], in2=BZ, in3=IR_q[2], in4=IR_q[3], out=open
  assign LADDR_3_8 = EN_ADDR_3_8 ? {IR_q_3, IR_q_2} : 8'bz;  // Controlled_Buffer controlled_buffer_5
  assign LADDR_3_8 = EN_ADDR_8_3 ? {IR_q_4[2:0], IR_q_3, IR_q_2[3]} : 8'bz;  // Controlled_Buffer controlled_buffer_6
  and and_4 (BC, alu_1_cf, IR_q[0], BZ, ~IR_q[2], IR_q[3]);  // AND_Gate
  // Probe on Rd_MUX
  Multiplexer #(.width(3)) multiplexer_4 (
    .in0({IR_q_3[1:0], IR_q_2[3]}), .in1(IR_q_4[2:0]), .out(Rd_MUX), .sel(and_5_out));
  assign ALU_RESULT = EN_IMM ? {IR_q_3, IR_q_2} : 8'bz;  // Controlled_Buffer controlled_buffer_7
  and and_5 (and_5_out, ~IR_q[3], ~IR_q[2], BZ);  // AND_Gate

  // Other names for the same wires on the sheet: IMM[7:0] = ALU_RESULT; LADDR_8_3[7:0] = LADDR_3_8;
  //   OE_RAM = mem_out_en; WE_RAM = mem_write_en

  // Notes on the sheet:
  //   Address Bus
  //   Data Bus
  //   Source
  //   CPU
  //   Destination
  //   BRANCH IS MADE WITH LOGIC, NO NEED SIGNALS
  //   For BRZ instruction 1010
  //   Other than that, the Rd (destination register) won't be used anyways
  //   For BRC instruction 1011
  //   Hear me out, if the opcode is 0001 (reg-to-reg), the select for Rd_MUX will be zero so it will be 3,3 path
  //   if the opcode is 0010 (imm-to-reg) OR 0011(mem-to-reg), the select will be one so it will be 3,8 path
  //   idk if this one is needed
endmodule
